// Logisim project CAESAR CIPHER ENCODER.circ as structural Verilog: 1 circuit, main circuit main
module main (
  input  [6:0] in_1,
  input  [2:0] KEY,
  input  in_3,
  output [6:0] out_4
);

  wire comparator_1_eq, comparator_1_gt, or_1_out;
  wire [6:0] adder_1_out, adder_2_out, multiplexer_1_out, subtractor_1_out;

  Hex_Digit_Display hex_digit_display_1 (.value(in_1[3:0]));  // open: dp
  Hex_Digit_Display hex_digit_display_2 (.value({1'b0, in_1[6:4]}));  // open: dp
  Adder #(.width(7)) adder_1 (.a(in_1), .b(7'b0111111), .out(adder_1_out));  // open: cin, cout
  Adder #(.width(7)) adder_2 (.a(adder_1_out), .b({4'b0000, KEY}), .out(adder_2_out));  // open: cin, cout
  Comparator #(.width(7)) comparator_1 (
    .a(adder_2_out), .b(7'b0011010), .gt(comparator_1_gt), .eq(comparator_1_eq));  // open: lt
  Subtractor #(.width(7)) subtractor_1 (.a(adder_2_out), .b(7'b0011010), .out(subtractor_1_out));  // open: bin, bout
  or or_1 (or_1_out, comparator_1_gt, comparator_1_eq);
  Multiplexer #(.width(7)) multiplexer_1 (
    .in0(adder_2_out), .in1(subtractor_1_out), .out(multiplexer_1_out), .sel(or_1_out), .en(in_3));
  Adder #(.width(7)) adder_3 (.a(multiplexer_1_out), .b(7'b1000001), .out(out_4));  // open: cin, cout
  Hex_Digit_Display hex_digit_display_3 (.value({1'b0, out_4[6:4]}));  // open: dp
  Hex_Digit_Display hex_digit_display_4 (.value(out_4[3:0]));  // open: dp

  // Notes on the sheet:
  //   7-Bit ASCII INPUT
  //   CONSTANT (2's Complement of -65)
  //   PADDING
  //   HEX DISPLAY (INPUT)
  //   CHAR INDEX
  //   CONSTANT (26)
  //   SHIFTED INDEX
  //   CONSTANT (65)
  //   MOD INDEX
  //   GE26
  //   FINAL   INDEX
  //   7-Bit ASCII OUTPUT
  //   HEX DISPLAY (OUTPUT)
endmodule
